// Logisim project 2a 3a.circ as structural Verilog: 1 circuit, main circuit main
module main (
  input  A1,
  input  A1_2,
  input  B1,
  input  B1_2,
  input  A2,
  input  A2_2,
  input  B2,
  input  B2_2,
  input  A3,
  input  A3_2,
  input  B3,
  input  B3_2,
  input  A4,
  input  A4_2,
  input  B4,
  input  B4_2,
  input  A5,
  input  A5_2,
  input  B5,
  input  A6,
  input  B5_2,
  input  B6,
  input  A6_2,
  input  A7,
  input  B6_2,
  input  B7,
  input  A7_2,
  input  A8,
  input  B7_2,
  input  B8,
  input  in_31,
  input  A8_2,
  input  B8_2
);

  wire and_1_out, and_2_out, and_3_out, and_4_out, and_5_out, and_6_out, and_7_out, and_8_out, and_9_out,
       and_10_out, and_11_out, and_12_out, and_13_out, and_14_out, and_15_out, and_16_out,
       controlled_buffer_1_out, controlled_buffer_2_out, controlled_buffer_3_out, controlled_buffer_4_out,
       controlled_buffer_5_out, controlled_buffer_6_out, controlled_buffer_7_out, controlled_buffer_8_out;

  and and_1 (and_1_out, A1, B1);
  and and_2 (and_2_out, A2_2, B2_2);
  and and_3 (and_3_out, A3_2, B3_2);
  and and_4 (and_4_out, A4_2, B4_2);
  and and_5 (and_5_out, A5_2, B5_2);
  and and_6 (and_6_out, A6_2, B6_2);
  and and_7 (and_7_out, A7_2, B7_2);
  and and_8 (and_8_out, A8_2, B8_2);
  LED led_1 (.in(and_1_out));
  LED led_2 (.in(and_2_out));
  LED led_3 (.in(and_3_out));
  LED led_4 (.in(and_4_out));
  LED led_5 (.in(and_5_out));
  LED led_6 (.in(and_6_out));
  LED led_7 (.in(and_7_out));
  LED led_8 (.in(and_8_out));
  and and_9 (and_9_out, A1_2, B1_2);
  and and_10 (and_10_out, A2, B2);
  and and_11 (and_11_out, A3, B3);
  and and_12 (and_12_out, A4, B4);
  and and_13 (and_13_out, A5, B5);
  and and_14 (and_14_out, A6, B6);
  and and_15 (and_15_out, A7, B7);
  and and_16 (and_16_out, A8, B8);
  assign controlled_buffer_1_out = in_31 ? and_9_out : 1'bz;  // Controlled_Buffer controlled_buffer_1
  assign controlled_buffer_2_out = in_31 ? and_10_out : 1'bz;  // Controlled_Buffer controlled_buffer_2
  assign controlled_buffer_3_out = in_31 ? and_11_out : 1'bz;  // Controlled_Buffer controlled_buffer_3
  assign controlled_buffer_4_out = in_31 ? and_12_out : 1'bz;  // Controlled_Buffer controlled_buffer_4
  assign controlled_buffer_5_out = in_31 ? and_13_out : 1'bz;  // Controlled_Buffer controlled_buffer_5
  assign controlled_buffer_6_out = in_31 ? and_14_out : 1'bz;  // Controlled_Buffer controlled_buffer_6
  assign controlled_buffer_7_out = in_31 ? and_15_out : 1'bz;  // Controlled_Buffer controlled_buffer_7
  assign controlled_buffer_8_out = in_31 ? and_16_out : 1'bz;  // Controlled_Buffer controlled_buffer_8
  LED led_9 (.in(controlled_buffer_1_out));
  LED led_10 (.in(controlled_buffer_2_out));
  LED led_11 (.in(controlled_buffer_3_out));
  LED led_12 (.in(controlled_buffer_4_out));
  LED led_13 (.in(controlled_buffer_5_out));
  LED led_14 (.in(controlled_buffer_6_out));
  LED led_15 (.in(controlled_buffer_7_out));
  LED led_16 (.in(controlled_buffer_8_out));
endmodule
