// Logisim project 2b 3b.circ as structural Verilog: 1 circuit, main circuit main
module main (
  input  in_1,
  input  in_2,
  input  in_3,
  input  in_4,
  input  in_5,
  input  in_6,
  input  in_7,
  input  in_8,
  input  in_9,
  input  in_10,
  input  in_11,
  input  in_12,
  input  in_13,
  input  in_14,
  input  in_15,
  input  in_16,
  input  in_17,
  input  in_18,
  input  in_19,
  input  in_20,
  input  in_21,
  input  in_22,
  input  in_23,
  input  in_24,
  input  in_25,
  input  in_26,
  input  in_27,
  input  in_28,
  input  in_29,
  input  in_30,
  input  in_31,
  input  in_32,
  input  in_33
);

  wire controlled_buffer_1_out, controlled_buffer_2_out, controlled_buffer_3_out, controlled_buffer_4_out,
       controlled_buffer_5_out, controlled_buffer_6_out, controlled_buffer_7_out, controlled_buffer_8_out,
       or_1_out, or_2_out, or_3_out, or_4_out, or_5_out, or_6_out, or_7_out, or_8_out, or_9_out, or_10_out,
       or_11_out, or_12_out, or_13_out, or_14_out, or_15_out, or_16_out;

  or or_1 (or_1_out, in_1, in_3);
  or or_2 (or_2_out, in_6, in_8);
  or or_3 (or_3_out, in_10, in_12);
  or or_4 (or_4_out, in_14, in_16);
  or or_5 (or_5_out, in_18, in_21);
  or or_6 (or_6_out, in_23, in_25);
  or or_7 (or_7_out, in_27, in_29);
  or or_8 (or_8_out, in_32, in_33);
  LED led_1 (.in(or_1_out));
  LED led_2 (.in(or_2_out));
  LED led_3 (.in(or_3_out));
  LED led_4 (.in(or_4_out));
  LED led_5 (.in(or_5_out));
  LED led_6 (.in(or_6_out));
  LED led_7 (.in(or_7_out));
  LED led_8 (.in(or_8_out));
  or or_9 (or_9_out, in_2, in_4);
  or or_10 (or_10_out, in_5, in_7);
  or or_11 (or_11_out, in_9, in_11);
  or or_12 (or_12_out, in_13, in_15);
  or or_13 (or_13_out, in_17, in_19);
  or or_14 (or_14_out, in_20, in_22);
  or or_15 (or_15_out, in_24, in_26);
  or or_16 (or_16_out, in_28, in_30);
  assign controlled_buffer_1_out = in_31 ? or_9_out : 1'bz;  // Controlled_Buffer controlled_buffer_1
  assign controlled_buffer_2_out = in_31 ? or_10_out : 1'bz;  // Controlled_Buffer controlled_buffer_2
  assign controlled_buffer_3_out = in_31 ? or_11_out : 1'bz;  // Controlled_Buffer controlled_buffer_3
  assign controlled_buffer_4_out = in_31 ? or_12_out : 1'bz;  // Controlled_Buffer controlled_buffer_4
  assign controlled_buffer_5_out = in_31 ? or_13_out : 1'bz;  // Controlled_Buffer controlled_buffer_5
  assign controlled_buffer_6_out = in_31 ? or_14_out : 1'bz;  // Controlled_Buffer controlled_buffer_6
  assign controlled_buffer_7_out = in_31 ? or_15_out : 1'bz;  // Controlled_Buffer controlled_buffer_7
  assign controlled_buffer_8_out = in_31 ? or_16_out : 1'bz;  // Controlled_Buffer controlled_buffer_8
  LED led_9 (.in(controlled_buffer_1_out));
  LED led_10 (.in(controlled_buffer_2_out));
  LED led_11 (.in(controlled_buffer_3_out));
  LED led_12 (.in(controlled_buffer_4_out));
  LED led_13 (.in(controlled_buffer_5_out));
  LED led_14 (.in(controlled_buffer_6_out));
  LED led_15 (.in(controlled_buffer_7_out));
  LED led_16 (.in(controlled_buffer_8_out));
endmodule
