// Logisim project 2c 3c.circ as structural Verilog: 1 circuit, main circuit main
module main (
  input  in_1,
  input  in_2,
  input  in_3,
  input  in_4,
  input  in_5,
  input  in_6,
  input  in_7,
  input  in_8,
  input  in_9,
  input  in_10,
  input  in_11,
  input  in_12,
  input  in_13,
  input  in_14,
  input  in_15,
  input  in_16,
  input  in_17
);

  wire controlled_buffer_1_out, controlled_buffer_2_out, controlled_buffer_3_out, controlled_buffer_4_out,
       controlled_buffer_5_out, controlled_buffer_6_out, controlled_buffer_7_out, controlled_buffer_8_out,
       not_1_out, not_2_out, not_3_out, not_4_out, not_5_out, not_6_out, not_7_out, not_8_out, not_9_out,
       not_10_out, not_11_out, not_12_out, not_13_out, not_14_out, not_15_out, not_16_out;

  not not_1 (not_1_out, in_1);
  not not_2 (not_2_out, in_3);
  not not_3 (not_3_out, in_5);
  not not_4 (not_4_out, in_7);
  not not_5 (not_5_out, in_9);
  not not_6 (not_6_out, in_11);
  not not_7 (not_7_out, in_13);
  not not_8 (not_8_out, in_15);
  LED led_1 (.in(not_1_out));
  LED led_2 (.in(not_2_out));
  LED led_3 (.in(not_3_out));
  LED led_4 (.in(not_4_out));
  LED led_5 (.in(not_5_out));
  LED led_6 (.in(not_6_out));
  LED led_7 (.in(not_7_out));
  LED led_8 (.in(not_8_out));
  not not_9 (not_9_out, in_2);
  not not_10 (not_10_out, in_4);
  not not_11 (not_11_out, in_6);
  not not_12 (not_12_out, in_8);
  not not_13 (not_13_out, in_10);
  not not_14 (not_14_out, in_12);
  not not_15 (not_15_out, in_14);
  not not_16 (not_16_out, in_16);
  assign controlled_buffer_1_out = in_17 ? not_9_out : 1'bz;  // Controlled_Buffer controlled_buffer_1
  assign controlled_buffer_2_out = in_17 ? not_10_out : 1'bz;  // Controlled_Buffer controlled_buffer_2
  assign controlled_buffer_3_out = in_17 ? not_11_out : 1'bz;  // Controlled_Buffer controlled_buffer_3
  assign controlled_buffer_4_out = in_17 ? not_12_out : 1'bz;  // Controlled_Buffer controlled_buffer_4
  assign controlled_buffer_5_out = in_17 ? not_13_out : 1'bz;  // Controlled_Buffer controlled_buffer_5
  assign controlled_buffer_6_out = in_17 ? not_14_out : 1'bz;  // Controlled_Buffer controlled_buffer_6
  assign controlled_buffer_7_out = in_17 ? not_15_out : 1'bz;  // Controlled_Buffer controlled_buffer_7
  assign controlled_buffer_8_out = in_17 ? not_16_out : 1'bz;  // Controlled_Buffer controlled_buffer_8
  LED led_9 (.in(controlled_buffer_1_out));
  LED led_10 (.in(controlled_buffer_2_out));
  LED led_11 (.in(controlled_buffer_3_out));
  LED led_12 (.in(controlled_buffer_4_out));
  LED led_13 (.in(controlled_buffer_5_out));
  LED led_14 (.in(controlled_buffer_6_out));
  LED led_15 (.in(controlled_buffer_7_out));
  LED led_16 (.in(controlled_buffer_8_out));
endmodule
