// Logisim project 2d 3d.circ as structural Verilog: 1 circuit, main circuit main
module main (
  input  in_1,
  input  in_2,
  input  in_3,
  input  in_4,
  input  in_5,
  input  in_6,
  input  in_7,
  input  in_8,
  input  in_9,
  input  in_10,
  input  in_11,
  input  in_12,
  input  in_13,
  input  in_14,
  input  in_15,
  input  in_16,
  input  in_17,
  input  in_18,
  input  in_19,
  input  in_20,
  input  in_21,
  input  in_22,
  input  in_23,
  input  in_24,
  input  in_25,
  input  in_26,
  input  in_27,
  input  in_28,
  input  in_29,
  input  in_30,
  input  in_31,
  input  in_32,
  input  in_33
);

  wire controlled_buffer_1_out, controlled_buffer_2_out, controlled_buffer_3_out, controlled_buffer_4_out,
       controlled_buffer_5_out, controlled_buffer_6_out, controlled_buffer_7_out, controlled_buffer_8_out,
       xor_1_out, xor_2_out, xor_3_out, xor_4_out, xor_5_out, xor_6_out, xor_7_out, xor_8_out, xor_9_out,
       xor_10_out, xor_11_out, xor_12_out, xor_13_out, xor_14_out, xor_15_out, xor_16_out;

  xor xor_1 (xor_1_out, in_1, in_3);
  xor xor_2 (xor_2_out, in_6, in_8);
  xor xor_3 (xor_3_out, in_10, in_12);
  xor xor_4 (xor_4_out, in_14, in_16);
  xor xor_5 (xor_5_out, in_18, in_21);
  xor xor_6 (xor_6_out, in_23, in_25);
  xor xor_7 (xor_7_out, in_27, in_29);
  xor xor_8 (xor_8_out, in_32, in_33);
  LED led_1 (.in(xor_1_out));
  LED led_2 (.in(xor_2_out));
  LED led_3 (.in(xor_3_out));
  LED led_4 (.in(xor_4_out));
  LED led_5 (.in(xor_5_out));
  LED led_6 (.in(xor_6_out));
  LED led_7 (.in(xor_7_out));
  LED led_8 (.in(xor_8_out));
  xor xor_9 (xor_9_out, in_2, in_4);
  xor xor_10 (xor_10_out, in_5, in_7);
  xor xor_11 (xor_11_out, in_9, in_11);
  xor xor_12 (xor_12_out, in_13, in_15);
  xor xor_13 (xor_13_out, in_17, in_19);
  xor xor_14 (xor_14_out, in_20, in_22);
  xor xor_15 (xor_15_out, in_24, in_26);
  xor xor_16 (xor_16_out, in_28, in_30);
  assign controlled_buffer_1_out = in_31 ? xor_9_out : 1'bz;  // Controlled_Buffer controlled_buffer_1
  assign controlled_buffer_2_out = in_31 ? xor_10_out : 1'bz;  // Controlled_Buffer controlled_buffer_2
  assign controlled_buffer_3_out = in_31 ? xor_11_out : 1'bz;  // Controlled_Buffer controlled_buffer_3
  assign controlled_buffer_4_out = in_31 ? xor_12_out : 1'bz;  // Controlled_Buffer controlled_buffer_4
  assign controlled_buffer_5_out = in_31 ? xor_13_out : 1'bz;  // Controlled_Buffer controlled_buffer_5
  assign controlled_buffer_6_out = in_31 ? xor_14_out : 1'bz;  // Controlled_Buffer controlled_buffer_6
  assign controlled_buffer_7_out = in_31 ? xor_15_out : 1'bz;  // Controlled_Buffer controlled_buffer_7
  assign controlled_buffer_8_out = in_31 ? xor_16_out : 1'bz;  // Controlled_Buffer controlled_buffer_8
  LED led_9 (.in(controlled_buffer_1_out));
  LED led_10 (.in(controlled_buffer_2_out));
  LED led_11 (.in(controlled_buffer_3_out));
  LED led_12 (.in(controlled_buffer_4_out));
  LED led_13 (.in(controlled_buffer_5_out));
  LED led_14 (.in(controlled_buffer_6_out));
  LED led_15 (.in(controlled_buffer_7_out));
  LED led_16 (.in(controlled_buffer_8_out));
endmodule
