// Logisim project 5.circ as structural Verilog: 3 circuits, main circuit main
module main (
  input  in_1,
  input  in_2,
  input  in_3,
  input  in_4,
  input  in_5,
  input  in_6,
  input  in_7,
  input  in_8,
  input  in_9,
  input  in_10,
  input  in_11,
  input  in_12,
  input  in_13,
  input  in_14,
  input  in_15,
  input  in_16,
  input  in_17,
  input  in_18,
  input  in_19,
  input  in_20,
  input  in_21,
  input  in_22,
  input  in_23,
  input  in_24,
  input  in_25,
  input  in_26,
  input  in_27,
  input  in_28,
  input  in_29,
  input  in_30,
  input  in_31,
  input  in_32,
  input  in_33,
  input  in_34,
  input  in_35,
  input  in_36,
  input  in_37,
  input  in_38,
  input  in_39,
  input  in_40,
  input  in_41,
  input  in_42,
  input  in_43,
  input  in_44,
  input  in_45,
  input  in_46,
  input  in_47,
  input  in_48,
  input  in_49,
  input  in_50,
  input  in_51,
  input  in_52,
  input  in_53,
  input  in_54,
  input  in_55,
  input  in_56,
  input  in_57,
  input  in_58,
  input  in_59,
  input  in_60,
  input  in_61,
  input  in_62,
  input  in_63,
  input  in_64,
  input  in_65,
  input  in_66,
  output out_67,
  output out_68,
  output out_69,
  output out_70,
  output out_71,
  output out_72,
  output out_73,
  output out_74,
  output out_75,
  output out_76,
  output out_77,
  output out_78,
  output out_79,
  output out_80,
  output out_81,
  output out_82,
  output out_83,
  output out_84,
  output out_85,
  output out_86,
  output out_87,
  output out_88,
  output out_89,
  output out_90,
  output out_91,
  output out_92,
  output out_93,
  output out_94,
  output out_95,
  output out_96,
  output out_97,
  output out_98
);

  wire gates_1_out_3, gates_1_out_4, gates_1_out_5, gates_1_out_6, gates_2_out_3, gates_2_out_4,
       gates_2_out_5, gates_2_out_6, gates_3_out_3, gates_3_out_4, gates_3_out_5, gates_3_out_6,
       gates_4_out_3, gates_4_out_4, gates_4_out_5, gates_4_out_6, gates_5_out_3, gates_5_out_4,
       gates_5_out_5, gates_5_out_6, gates_6_out_3, gates_6_out_4, gates_6_out_5, gates_6_out_6,
       gates_7_out_3, gates_7_out_4, gates_7_out_5, gates_7_out_6, gates_8_out_3, gates_8_out_4,
       gates_8_out_5, gates_8_out_6, gates_9_out_3, gates_9_out_4, gates_9_out_5, gates_9_out_6,
       gates_10_out_3, gates_10_out_4, gates_10_out_5, gates_10_out_6, gates_11_out_3, gates_11_out_4,
       gates_11_out_5, gates_11_out_6, gates_12_out_3, gates_12_out_4, gates_12_out_5, gates_12_out_6,
       gates_13_out_3, gates_13_out_4, gates_13_out_5, gates_13_out_6, gates_14_out_3, gates_14_out_4,
       gates_14_out_5, gates_14_out_6, gates_15_out_3, gates_15_out_4, gates_15_out_5, gates_15_out_6,
       gates_16_out_3, gates_16_out_4, gates_16_out_5, gates_16_out_6, gates_17_out_3, gates_17_out_4,
       gates_17_out_5, gates_17_out_6, gates_18_out_3, gates_18_out_4, gates_18_out_5, gates_18_out_6,
       gates_19_out_3, gates_19_out_4, gates_19_out_5, gates_19_out_6, gates_20_out_3, gates_20_out_4,
       gates_20_out_5, gates_20_out_6, gates_21_out_3, gates_21_out_4, gates_21_out_5, gates_21_out_6,
       gates_22_out_3, gates_22_out_4, gates_22_out_5, gates_22_out_6, gates_23_out_3, gates_23_out_4,
       gates_23_out_5, gates_23_out_6, gates_24_out_3, gates_24_out_4, gates_24_out_5, gates_24_out_6,
       gates_25_out_3, gates_25_out_4, gates_25_out_5, gates_25_out_6, gates_26_out_3, gates_26_out_4,
       gates_26_out_5, gates_26_out_6, gates_27_out_3, gates_27_out_4, gates_27_out_5, gates_27_out_6,
       gates_28_out_3, gates_28_out_4, gates_28_out_5, gates_28_out_6, gates_29_out_3, gates_29_out_4,
       gates_29_out_5, gates_29_out_6, gates_30_out_3, gates_30_out_4, gates_30_out_5, gates_30_out_6,
       gates_31_out_3, gates_31_out_4, gates_31_out_5, gates_31_out_6, gates_32_out_3, gates_32_out_4,
       gates_32_out_5, gates_32_out_6;

  Gates gates_1 (
    .in_1(in_1), .in_2(in_5), .out_3(gates_1_out_3), .out_4(gates_1_out_4), .out_5(gates_1_out_5),
    .out_6(gates_1_out_6));
  Gates gates_2 (
    .in_1(in_9), .in_2(in_13), .out_3(gates_2_out_3), .out_4(gates_2_out_4), .out_5(gates_2_out_5),
    .out_6(gates_2_out_6));
  Gates gates_3 (
    .in_1(in_17), .in_2(in_21), .out_3(gates_3_out_3), .out_4(gates_3_out_4), .out_5(gates_3_out_5),
    .out_6(gates_3_out_6));
  Gates gates_4 (
    .in_1(in_25), .in_2(in_29), .out_3(gates_4_out_3), .out_4(gates_4_out_4), .out_5(gates_4_out_5),
    .out_6(gates_4_out_6));
  Gates gates_5 (
    .in_1(in_33), .in_2(in_37), .out_3(gates_5_out_3), .out_4(gates_5_out_4), .out_5(gates_5_out_5),
    .out_6(gates_5_out_6));
  Gates gates_6 (
    .in_1(in_41), .in_2(in_45), .out_3(gates_6_out_3), .out_4(gates_6_out_4), .out_5(gates_6_out_5),
    .out_6(gates_6_out_6));
  Gates gates_7 (
    .in_1(in_49), .in_2(in_53), .out_3(gates_7_out_3), .out_4(gates_7_out_4), .out_5(gates_7_out_5),
    .out_6(gates_7_out_6));
  Gates gates_8 (
    .in_1(in_57), .in_2(in_61), .out_3(gates_8_out_3), .out_4(gates_8_out_4), .out_5(gates_8_out_5),
    .out_6(gates_8_out_6));
  _4X1_MUX u_4x1_mux_1 (
    .in_1(gates_1_out_3), .in_2(gates_1_out_4), .in_3(gates_1_out_5), .in_4(gates_1_out_6), .out_7(out_67),
    .in_5(in_65), .in_6(in_66));
  _4X1_MUX u_4x1_mux_2 (
    .in_1(gates_2_out_3), .in_2(gates_2_out_4), .in_3(gates_2_out_5), .in_4(gates_2_out_6), .out_7(out_71),
    .in_5(in_65), .in_6(in_66));
  _4X1_MUX u_4x1_mux_3 (
    .in_1(gates_3_out_3), .in_2(gates_3_out_4), .in_3(gates_3_out_5), .in_4(gates_3_out_6), .out_7(out_75),
    .in_5(in_65), .in_6(in_66));
  _4X1_MUX u_4x1_mux_4 (
    .in_1(gates_4_out_3), .in_2(gates_4_out_4), .in_3(gates_4_out_5), .in_4(gates_4_out_6), .out_7(out_79),
    .in_5(in_65), .in_6(in_66));
  _4X1_MUX u_4x1_mux_5 (
    .in_1(gates_5_out_3), .in_2(gates_5_out_4), .in_3(gates_5_out_5), .in_4(gates_5_out_6), .out_7(out_83),
    .in_5(in_65), .in_6(in_66));
  _4X1_MUX u_4x1_mux_6 (
    .in_1(gates_6_out_3), .in_2(gates_6_out_4), .in_3(gates_6_out_5), .in_4(gates_6_out_6), .out_7(out_87),
    .in_5(in_65), .in_6(in_66));
  _4X1_MUX u_4x1_mux_7 (
    .in_1(gates_7_out_3), .in_2(gates_7_out_4), .in_3(gates_7_out_5), .in_4(gates_7_out_6), .out_7(out_91),
    .in_5(in_65), .in_6(in_66));
  _4X1_MUX u_4x1_mux_8 (
    .in_1(gates_8_out_3), .in_2(gates_8_out_4), .in_3(gates_8_out_5), .in_4(gates_8_out_6), .out_7(out_95),
    .in_5(in_65), .in_6(in_66));
  Gates gates_9 (
    .in_1(in_2), .in_2(in_6), .out_3(gates_9_out_3), .out_4(gates_9_out_4), .out_5(gates_9_out_5),
    .out_6(gates_9_out_6));
  Gates gates_10 (
    .in_1(in_10), .in_2(in_14), .out_3(gates_10_out_3), .out_4(gates_10_out_4), .out_5(gates_10_out_5),
    .out_6(gates_10_out_6));
  Gates gates_11 (
    .in_1(in_18), .in_2(in_22), .out_3(gates_11_out_3), .out_4(gates_11_out_4), .out_5(gates_11_out_5),
    .out_6(gates_11_out_6));
  Gates gates_12 (
    .in_1(in_26), .in_2(in_30), .out_3(gates_12_out_3), .out_4(gates_12_out_4), .out_5(gates_12_out_5),
    .out_6(gates_12_out_6));
  Gates gates_13 (
    .in_1(in_34), .in_2(in_38), .out_3(gates_13_out_3), .out_4(gates_13_out_4), .out_5(gates_13_out_5),
    .out_6(gates_13_out_6));
  Gates gates_14 (
    .in_1(in_42), .in_2(in_46), .out_3(gates_14_out_3), .out_4(gates_14_out_4), .out_5(gates_14_out_5),
    .out_6(gates_14_out_6));
  Gates gates_15 (
    .in_1(in_50), .in_2(in_54), .out_3(gates_15_out_3), .out_4(gates_15_out_4), .out_5(gates_15_out_5),
    .out_6(gates_15_out_6));
  Gates gates_16 (
    .in_1(in_58), .in_2(in_62), .out_3(gates_16_out_3), .out_4(gates_16_out_4), .out_5(gates_16_out_5),
    .out_6(gates_16_out_6));
  _4X1_MUX u_4x1_mux_9 (
    .in_1(gates_9_out_3), .in_2(gates_9_out_4), .in_3(gates_9_out_5), .in_4(gates_9_out_6), .out_7(out_68),
    .in_5(in_65), .in_6(in_66));
  _4X1_MUX u_4x1_mux_10 (
    .in_1(gates_10_out_3), .in_2(gates_10_out_4), .in_3(gates_10_out_5), .in_4(gates_10_out_6),
    .out_7(out_72), .in_5(in_65), .in_6(in_66));
  _4X1_MUX u_4x1_mux_11 (
    .in_1(gates_11_out_3), .in_2(gates_11_out_4), .in_3(gates_11_out_5), .in_4(gates_11_out_6),
    .out_7(out_76), .in_5(in_65), .in_6(in_66));
  _4X1_MUX u_4x1_mux_12 (
    .in_1(gates_12_out_3), .in_2(gates_12_out_4), .in_3(gates_12_out_5), .in_4(gates_12_out_6),
    .out_7(out_80), .in_5(in_65), .in_6(in_66));
  _4X1_MUX u_4x1_mux_13 (
    .in_1(gates_13_out_3), .in_2(gates_13_out_4), .in_3(gates_13_out_5), .in_4(gates_13_out_6),
    .out_7(out_84), .in_5(in_65), .in_6(in_66));
  _4X1_MUX u_4x1_mux_14 (
    .in_1(gates_14_out_3), .in_2(gates_14_out_4), .in_3(gates_14_out_5), .in_4(gates_14_out_6),
    .out_7(out_88), .in_5(in_65), .in_6(in_66));
  _4X1_MUX u_4x1_mux_15 (
    .in_1(gates_15_out_3), .in_2(gates_15_out_4), .in_3(gates_15_out_5), .in_4(gates_15_out_6),
    .out_7(out_92), .in_5(in_65), .in_6(in_66));
  _4X1_MUX u_4x1_mux_16 (
    .in_1(gates_16_out_3), .in_2(gates_16_out_4), .in_3(gates_16_out_5), .in_4(gates_16_out_6),
    .out_7(out_96), .in_5(in_65), .in_6(in_66));
  Gates gates_17 (
    .in_1(in_3), .in_2(in_7), .out_3(gates_17_out_3), .out_4(gates_17_out_4), .out_5(gates_17_out_5),
    .out_6(gates_17_out_6));
  Gates gates_18 (
    .in_1(in_11), .in_2(in_15), .out_3(gates_18_out_3), .out_4(gates_18_out_4), .out_5(gates_18_out_5),
    .out_6(gates_18_out_6));
  Gates gates_19 (
    .in_1(in_19), .in_2(in_23), .out_3(gates_19_out_3), .out_4(gates_19_out_4), .out_5(gates_19_out_5),
    .out_6(gates_19_out_6));
  Gates gates_20 (
    .in_1(in_27), .in_2(in_31), .out_3(gates_20_out_3), .out_4(gates_20_out_4), .out_5(gates_20_out_5),
    .out_6(gates_20_out_6));
  Gates gates_21 (
    .in_1(in_35), .in_2(in_39), .out_3(gates_21_out_3), .out_4(gates_21_out_4), .out_5(gates_21_out_5),
    .out_6(gates_21_out_6));
  Gates gates_22 (
    .in_1(in_43), .in_2(in_47), .out_3(gates_22_out_3), .out_4(gates_22_out_4), .out_5(gates_22_out_5),
    .out_6(gates_22_out_6));
  Gates gates_23 (
    .in_1(in_51), .in_2(in_55), .out_3(gates_23_out_3), .out_4(gates_23_out_4), .out_5(gates_23_out_5),
    .out_6(gates_23_out_6));
  Gates gates_24 (
    .in_1(in_59), .in_2(in_63), .out_3(gates_24_out_3), .out_4(gates_24_out_4), .out_5(gates_24_out_5),
    .out_6(gates_24_out_6));
  _4X1_MUX u_4x1_mux_17 (
    .in_1(gates_17_out_3), .in_2(gates_17_out_4), .in_3(gates_17_out_5), .in_4(gates_17_out_6),
    .out_7(out_69), .in_5(in_65), .in_6(in_66));
  _4X1_MUX u_4x1_mux_18 (
    .in_1(gates_18_out_3), .in_2(gates_18_out_4), .in_3(gates_18_out_5), .in_4(gates_18_out_6),
    .out_7(out_73), .in_5(in_65), .in_6(in_66));
  _4X1_MUX u_4x1_mux_19 (
    .in_1(gates_19_out_3), .in_2(gates_19_out_4), .in_3(gates_19_out_5), .in_4(gates_19_out_6),
    .out_7(out_77), .in_5(in_65), .in_6(in_66));
  _4X1_MUX u_4x1_mux_20 (
    .in_1(gates_20_out_3), .in_2(gates_20_out_4), .in_3(gates_20_out_5), .in_4(gates_20_out_6),
    .out_7(out_81), .in_5(in_65), .in_6(in_66));
  _4X1_MUX u_4x1_mux_21 (
    .in_1(gates_21_out_3), .in_2(gates_21_out_4), .in_3(gates_21_out_5), .in_4(gates_21_out_6),
    .out_7(out_85), .in_5(in_65), .in_6(in_66));
  _4X1_MUX u_4x1_mux_22 (
    .in_1(gates_22_out_3), .in_2(gates_22_out_4), .in_3(gates_22_out_5), .in_4(gates_22_out_6),
    .out_7(out_89), .in_5(in_65), .in_6(in_66));
  _4X1_MUX u_4x1_mux_23 (
    .in_1(gates_23_out_3), .in_2(gates_23_out_4), .in_3(gates_23_out_5), .in_4(gates_23_out_6),
    .out_7(out_93), .in_5(in_65), .in_6(in_66));
  _4X1_MUX u_4x1_mux_24 (
    .in_1(gates_24_out_3), .in_2(gates_24_out_4), .in_3(gates_24_out_5), .in_4(gates_24_out_6),
    .out_7(out_97), .in_5(in_65), .in_6(in_66));
  Gates gates_25 (
    .in_1(in_4), .in_2(in_8), .out_3(gates_25_out_3), .out_4(gates_25_out_4), .out_5(gates_25_out_5),
    .out_6(gates_25_out_6));
  Gates gates_26 (
    .in_1(in_12), .in_2(in_16), .out_3(gates_26_out_3), .out_4(gates_26_out_4), .out_5(gates_26_out_5),
    .out_6(gates_26_out_6));
  Gates gates_27 (
    .in_1(in_20), .in_2(in_24), .out_3(gates_27_out_3), .out_4(gates_27_out_4), .out_5(gates_27_out_5),
    .out_6(gates_27_out_6));
  Gates gates_28 (
    .in_1(in_28), .in_2(in_32), .out_3(gates_28_out_3), .out_4(gates_28_out_4), .out_5(gates_28_out_5),
    .out_6(gates_28_out_6));
  Gates gates_29 (
    .in_1(in_36), .in_2(in_40), .out_3(gates_29_out_3), .out_4(gates_29_out_4), .out_5(gates_29_out_5),
    .out_6(gates_29_out_6));
  Gates gates_30 (
    .in_1(in_44), .in_2(in_48), .out_3(gates_30_out_3), .out_4(gates_30_out_4), .out_5(gates_30_out_5),
    .out_6(gates_30_out_6));
  Gates gates_31 (
    .in_1(in_52), .in_2(in_56), .out_3(gates_31_out_3), .out_4(gates_31_out_4), .out_5(gates_31_out_5),
    .out_6(gates_31_out_6));
  Gates gates_32 (
    .in_1(in_60), .in_2(in_64), .out_3(gates_32_out_3), .out_4(gates_32_out_4), .out_5(gates_32_out_5),
    .out_6(gates_32_out_6));
  _4X1_MUX u_4x1_mux_25 (
    .in_1(gates_25_out_3), .in_2(gates_25_out_4), .in_3(gates_25_out_5), .in_4(gates_25_out_6),
    .out_7(out_70), .in_5(in_65), .in_6(in_66));
  _4X1_MUX u_4x1_mux_26 (
    .in_1(gates_26_out_3), .in_2(gates_26_out_4), .in_3(gates_26_out_5), .in_4(gates_26_out_6),
    .out_7(out_74), .in_5(in_65), .in_6(in_66));
  _4X1_MUX u_4x1_mux_27 (
    .in_1(gates_27_out_3), .in_2(gates_27_out_4), .in_3(gates_27_out_5), .in_4(gates_27_out_6),
    .out_7(out_78), .in_5(in_65), .in_6(in_66));
  _4X1_MUX u_4x1_mux_28 (
    .in_1(gates_28_out_3), .in_2(gates_28_out_4), .in_3(gates_28_out_5), .in_4(gates_28_out_6),
    .out_7(out_82), .in_5(in_65), .in_6(in_66));
  _4X1_MUX u_4x1_mux_29 (
    .in_1(gates_29_out_3), .in_2(gates_29_out_4), .in_3(gates_29_out_5), .in_4(gates_29_out_6),
    .out_7(out_86), .in_5(in_65), .in_6(in_66));
  _4X1_MUX u_4x1_mux_30 (
    .in_1(gates_30_out_3), .in_2(gates_30_out_4), .in_3(gates_30_out_5), .in_4(gates_30_out_6),
    .out_7(out_90), .in_5(in_65), .in_6(in_66));
  _4X1_MUX u_4x1_mux_31 (
    .in_1(gates_31_out_3), .in_2(gates_31_out_4), .in_3(gates_31_out_5), .in_4(gates_31_out_6),
    .out_7(out_94), .in_5(in_65), .in_6(in_66));
  _4X1_MUX u_4x1_mux_32 (
    .in_1(gates_32_out_3), .in_2(gates_32_out_4), .in_3(gates_32_out_5), .in_4(gates_32_out_6),
    .out_7(out_98), .in_5(in_65), .in_6(in_66));

  // Notes on the sheet:
  //   LEGEND
  //   1-AND
  //   2-OR
  //   3-NOT
  //   4-XOR
endmodule

module _4X1_MUX (
  input  in_1,
  input  in_2,
  input  in_3,
  input  in_4,
  input  in_5,
  input  in_6,
  output out_7
);

  wire and_1_out, and_2_out, and_3_out, and_4_out, not_1_out, not_2_out;

  not not_1 (not_1_out, in_5);
  not not_2 (not_2_out, in_6);
  and and_1 (and_1_out, in_1, in_5, in_6);
  and and_2 (and_2_out, in_2, in_5, not_2_out);
  and and_3 (and_3_out, in_3, not_1_out, in_6);
  and and_4 (and_4_out, in_4, not_1_out, not_2_out);
  or or_1 (out_7, and_1_out, and_2_out, and_3_out, and_4_out);
endmodule

module Gates (
  input  in_1,
  input  in_2,
  output out_3,
  output out_4,
  output out_5,
  output out_6
);

  and and_1 (out_3, in_1, in_2);
  or or_1 (out_4, in_1, in_2);
  not not_1 (out_5, in_1);
  xor xor_1 (out_6, in_1, in_2);
endmodule
