// Logisim project 6.circ as structural Verilog: 2 circuits, main circuit main
module main (
  input  X0,
  input  X1,
  input  X2,
  input  X3,
  input  SHIFT_COUNT,
  input  in_6,
  output Y3,
  output Y2,
  output Y1,
  output Y0
);

  wire decoder_1_out_3, decoder_1_out_4, decoder_1_out_5, decoder_1_out_6;

  Decoder decoder_1 (
    .in_1(SHIFT_COUNT), .in_2(in_6), .out_3(decoder_1_out_3), .out_4(decoder_1_out_4),
    .out_5(decoder_1_out_5), .out_6(decoder_1_out_6));
  assign Y3 = decoder_1_out_3 ? X0 : 1'bz;  // Controlled_Buffer controlled_buffer_1
  assign Y2 = decoder_1_out_4 ? X0 : 1'bz;  // Controlled_Buffer controlled_buffer_2
  assign Y1 = decoder_1_out_5 ? X0 : 1'bz;  // Controlled_Buffer controlled_buffer_3
  assign Y0 = decoder_1_out_6 ? X0 : 1'bz;  // Controlled_Buffer controlled_buffer_4
  assign Y3 = decoder_1_out_4 ? X1 : 1'bz;  // Controlled_Buffer controlled_buffer_5
  assign Y2 = decoder_1_out_5 ? X1 : 1'bz;  // Controlled_Buffer controlled_buffer_6
  assign Y1 = decoder_1_out_6 ? X1 : 1'bz;  // Controlled_Buffer controlled_buffer_7
  assign Y0 = decoder_1_out_3 ? X1 : 1'bz;  // Controlled_Buffer controlled_buffer_8
  assign Y3 = decoder_1_out_5 ? X2 : 1'bz;  // Controlled_Buffer controlled_buffer_9
  assign Y2 = decoder_1_out_6 ? X2 : 1'bz;  // Controlled_Buffer controlled_buffer_10
  assign Y1 = decoder_1_out_3 ? X2 : 1'bz;  // Controlled_Buffer controlled_buffer_11
  assign Y0 = decoder_1_out_4 ? X2 : 1'bz;  // Controlled_Buffer controlled_buffer_12
  assign Y3 = decoder_1_out_6 ? X3 : 1'bz;  // Controlled_Buffer controlled_buffer_13
  assign Y2 = decoder_1_out_3 ? X3 : 1'bz;  // Controlled_Buffer controlled_buffer_14
  assign Y1 = decoder_1_out_4 ? X3 : 1'bz;  // Controlled_Buffer controlled_buffer_15
  assign Y0 = decoder_1_out_5 ? X3 : 1'bz;  // Controlled_Buffer controlled_buffer_16
endmodule

module Decoder (
  input  in_1,
  input  in_2,
  output out_3,
  output out_4,
  output out_5,
  output out_6
);

  wire not_1_out, not_2_out;

  not not_1 (not_1_out, in_1);
  not not_2 (not_2_out, in_2);
  and and_1 (out_3, in_1, in_2);
  and and_2 (out_4, in_1, not_2_out);
  and and_3 (out_5, not_1_out, in_2);
  and and_4 (out_6, not_1_out, not_2_out);
endmodule
