// Logisim project 7.circ as structural Verilog: 2 circuits, main circuit main
module main (
  input  B3,
  input  A3,
  input  B2,
  input  A2,
  input  B1,
  input  A1,
  input  B0,
  input  A0,
  output Final_Carry,
  output S3,
  output S2,
  output S1,
  output S0
);

  wire full_adder_2_out_5, full_adder_3_out_5, full_adder_4_out_5;

  FULL_ADDER full_adder_1 (.in_1(A3), .in_2(B3), .in_3(full_adder_2_out_5), .out_4(S3), .out_5(Final_Carry));
  FULL_ADDER full_adder_2 (.in_1(A2), .in_2(B2), .in_3(full_adder_3_out_5), .out_4(S2), .out_5(full_adder_2_out_5));
  FULL_ADDER full_adder_3 (.in_1(A1), .in_2(B1), .in_3(full_adder_4_out_5), .out_4(S1), .out_5(full_adder_3_out_5));
  FULL_ADDER full_adder_4 (.in_1(A0), .in_2(B0), .in_3(1'b0), .out_4(S0), .out_5(full_adder_4_out_5));
endmodule

module FULL_ADDER (
  input  in_1,
  input  in_2,
  input  in_3,
  output out_4,
  output out_5
);

  wire and_1_out, and_2_out, xor_1_out;

  xor xor_1 (xor_1_out, in_1, in_2);
  xor xor_2 (out_4, xor_1_out, in_3);
  and and_1 (and_1_out, xor_1_out, in_3);
  and and_2 (and_2_out, in_2, in_1);
  or or_1 (out_5, and_1_out, and_2_out);
endmodule
