// Logisim project 8.circ as structural Verilog: 2 circuits, main circuit main
module main (
  input  in_1,
  input  in_2,
  input  in_3,
  input  in_4,
  input  in_5,
  input  in_6,
  output out_7,
  output out_8
);

  _8X1_MUX u_8x1_mux_1 (
    .I7(1'b1), .I6(1'b0), .I5(1'b0), .I4(1'b0), .I3(1'b0), .I2(1'b0), .I1(1'b0), .I0(1'b0), .out_12(out_7),
    .S2(in_1), .S1(in_2), .S0(in_3));
  _8X1_MUX u_8x1_mux_2 (
    .I7(1'b1), .I6(1'b1), .I5(1'b1), .I4(1'b1), .I3(1'b1), .I2(1'b1), .I1(1'b1), .I0(1'b0), .out_12(out_8),
    .S2(in_4), .S1(in_5), .S0(in_6));

  // Notes on the sheet:
  //   3-INPUT AND GATE
  //   3-INPUT OR GATE
endmodule

module _8X1_MUX (
  input  I7,
  input  I6,
  input  I5,
  input  I4,
  input  I3,
  input  I2,
  input  I1,
  input  I0,
  input  S2,
  input  S1,
  input  S0,
  output out_12
);

  wire and_1_out, and_2_out, and_3_out, and_4_out, and_5_out, and_6_out, and_7_out, and_8_out, not_1_out,
       not_2_out, not_3_out;

  not not_1 (not_1_out, S2);
  not not_2 (not_2_out, S1);
  not not_3 (not_3_out, S0);
  and and_1 (and_1_out, I7, S2, S1, S0);
  and and_2 (and_2_out, I6, S2, S1, not_3_out);
  and and_3 (and_3_out, I5, S2, not_2_out, S0);
  and and_4 (and_4_out, I4, S2, not_2_out, not_3_out);
  and and_5 (and_5_out, I3, not_1_out, S1, S0);
  and and_6 (and_6_out, I2, not_1_out, S1, not_3_out);
  and and_7 (and_7_out, I1, not_1_out, not_2_out, S0);
  and and_8 (and_8_out, I0, not_1_out, not_2_out, not_3_out);
  or or_1 (out_12, and_1_out, and_2_out, and_3_out, and_4_out, and_5_out, and_6_out, and_7_out, and_8_out);
endmodule
