// Logisim project half adder.circ as structural Verilog: 2 circuits, main circuit main
module main (
  input  A,
  input  B,
  output SUM,
  output CARRY,
  output SUM_2,
  output CARRY_2
);

  wire nand_1_out, nand_2_out, nand_3_out;

  xor xor_1 (SUM, A, B);
  and and_1 (CARRY, A, B);
  nand nand_1 (nand_1_out, A, B);
  nand nand_2 (nand_2_out, A, nand_1_out);
  nand nand_3 (nand_3_out, nand_1_out, B);
  nand nand_4 (SUM_2, nand_2_out, nand_3_out);
  nand nand_5 (CARRY_2, nand_1_out, nand_1_out);
endmodule

module _8X1_MUX (
  input  I7,
  input  I6,
  input  I5,
  input  I4,
  input  I3,
  input  I2,
  input  I1,
  input  I0,
  input  S2,
  input  S1,
  input  S0,
  output out_12
);

  wire and_1_out, and_2_out, and_3_out, and_4_out, and_5_out, and_6_out, and_7_out, and_8_out, not_1_out,
       not_2_out, not_3_out;

  not not_1 (not_1_out, S2);
  not not_2 (not_2_out, S1);
  not not_3 (not_3_out, S0);
  and and_1 (and_1_out, I7, S2, S1, S0);
  and and_2 (and_2_out, I6, S2, S1, not_3_out);
  and and_3 (and_3_out, I5, S2, not_2_out, S0);
  and and_4 (and_4_out, I4, S2, not_2_out, not_3_out);
  and and_5 (and_5_out, I3, not_1_out, S1, S0);
  and and_6 (and_6_out, I2, not_1_out, S1, not_3_out);
  and and_7 (and_7_out, I1, not_1_out, not_2_out, S0);
  and and_8 (and_8_out, I0, not_1_out, not_2_out, not_3_out);
  or or_1 (out_12, and_1_out, and_2_out, and_3_out, and_4_out, and_5_out, and_6_out, and_7_out, and_8_out);
endmodule
